// Digital circuit ALU_Control.dig as structural Verilog
module ALU_Control (
  input  [5:0] Func,
  output [2:0] ALUFunc
);

  ROM #(.AddrBits(6), .Bits(3)) AluControl (.A(Func), .sel(1'b1), .D(ALUFunc));

  // Notes on the sheet:
  //   contents of AluControl (hex, n*v repeats v):
  //   0,0,0,0,0,0,0,0,0,0,0,0,0,0,0,0,0,0,0,0,0,0,0,0,0,0,0,0,0,0,0,0,0,0,1,0,2,3,5,0,0,
  //   0,4
endmodule
